// Logisim project ula.circ as structural Verilog: 7 circuits, main circuit ULA_8bits
module ULA_8bits (
  input  [7:0] E1,
  input  [7:0] E2,
  input  s0,
  input  s1,
  input  s2,
  output [7:0] Z
);

  wire [7:0] and_1_out, nand_1_out, nor_1_out, or_1_out, somador_8bits_1_soma, subtrator_8bits_1_subtracao;

  subtrator_8bits subtrator_8bits_1 (.A(E1), .B(E2), .SUBTRACAO(subtrator_8bits_1_subtracao));  // open: Borrow
  somador_8bits somador_8bits_1 (.A(E1), .B(E2), .SOMA(somador_8bits_1_soma));  // open: Vai_um
  assign and_1_out = E2 & E1;  // AND_Gate and_1, 8 bits wide
  assign nor_1_out = ~(E2 | E1);  // NOR_Gate nor_1, 8 bits wide
  multiplexador multiplexador_1 (
    .I0(or_1_out), .I1(nand_1_out), .I2(nor_1_out), .I3(and_1_out), .L4(somador_8bits_1_soma),
    .I5(subtrator_8bits_1_subtracao), .S2(s2), .S1(s1), .S0(s0), .Z(Z));  // open: L6, L7
  assign nand_1_out = ~(E2 & E1);  // NAND_Gate nand_1, 8 bits wide
  assign or_1_out = E2 | E1;  // OR_Gate or_1, 8 bits wide

  // Notes on the sheet:
  //   sendo S0 o menor BIt
endmodule

module somador_1bit (
  input  in_1,
  input  in_2,
  input  in_3,
  output out_4,
  output out_5
);

  wire and_1_out, and_2_out, and_3_out, xor_1_out;

  xor xor_1 (xor_1_out, in_2, in_3);
  and and_1 (and_1_out, in_2, in_3);
  and and_2 (and_2_out, in_2, in_1);
  and and_3 (and_3_out, in_2, in_1);
  xor xor_2 (out_4, in_1, xor_1_out);
  or or_1 (out_5, and_1_out, and_2_out, and_3_out);

  // Notes on the sheet:
  //   A
  //   B
  //   CIN
  //   S = A XOR B X CIN
  //   COUT = ACIN + BCIN + AB
endmodule

module somador_8bits (
  input  [7:0] A,
  input  [7:0] B,
  output [7:0] SOMA,
  output Vai_um
);

  wire somador_1bit_1_out_5, somador_1bit_2_out_5, somador_1bit_3_out_5, somador_1bit_4_out_5,
       somador_1bit_5_out_5, somador_1bit_6_out_5, somador_1bit_7_out_5;

  somador_1bit somador_1bit_1 (.in_1(A[0]), .in_2(B[0]), .out_4(SOMA[0]), .out_5(somador_1bit_1_out_5));  // open: in_3
  somador_1bit somador_1bit_2 (
    .in_1(A[1]), .in_2(B[1]), .in_3(somador_1bit_1_out_5), .out_4(SOMA[1]), .out_5(somador_1bit_2_out_5));
  somador_1bit somador_1bit_3 (
    .in_1(A[2]), .in_2(B[2]), .in_3(somador_1bit_2_out_5), .out_4(SOMA[2]), .out_5(somador_1bit_3_out_5));
  somador_1bit somador_1bit_4 (
    .in_1(A[3]), .in_2(B[3]), .in_3(somador_1bit_3_out_5), .out_4(SOMA[3]), .out_5(somador_1bit_4_out_5));
  somador_1bit somador_1bit_5 (
    .in_1(A[4]), .in_2(B[4]), .in_3(somador_1bit_4_out_5), .out_4(SOMA[4]), .out_5(somador_1bit_5_out_5));
  somador_1bit somador_1bit_6 (
    .in_1(A[5]), .in_2(B[5]), .in_3(somador_1bit_5_out_5), .out_4(SOMA[5]), .out_5(somador_1bit_6_out_5));
  somador_1bit somador_1bit_7 (
    .in_1(A[6]), .in_2(B[6]), .in_3(somador_1bit_6_out_5), .out_4(SOMA[6]), .out_5(somador_1bit_7_out_5));
  somador_1bit somador_1bit_8 (.in_1(A[7]), .in_2(B[7]), .in_3(somador_1bit_7_out_5), .out_4(SOMA[7]), .out_5(Vai_um));

  // Notes on the sheet:
  //   Somador 1
  //   Somador 2
  //   Somador 3
  //   Somador 4
  //   Somador 5
  //   Somador 6
  //   Somador 7
  //   Somador 8
endmodule

module subtrator (
  input  A,
  input  B,
  input  T,
  output S,
  output Tout
);

  wire and_1_out, and_2_out, and_3_out, not_1_out, not_2_out, xor_1_out;

  not not_1 (not_1_out, A);
  not not_2 (not_2_out, A);
  xor xor_1 (xor_1_out, A, B);
  and and_1 (and_1_out, B, T);
  and and_2 (and_2_out, T, not_2_out);
  and and_3 (and_3_out, B, not_1_out);
  xor xor_2 (S, xor_1_out, T);
  or or_1 (Tout, and_1_out, and_2_out, and_3_out);
endmodule

module subtrator_8bits (
  input  [7:0] A,
  input  [7:0] B,
  output [7:0] SUBTRACAO,
  output Borrow
);

  wire subtrator_1_tout, subtrator_2_tout, subtrator_3_tout, subtrator_4_tout, subtrator_5_tout,
       subtrator_6_tout, subtrator_7_tout;

  subtrator subtrator_1 (.A(A[0]), .B(B[0]), .S(SUBTRACAO[0]), .Tout(subtrator_1_tout));  // open: T
  subtrator subtrator_2 (.A(A[1]), .B(B[1]), .T(subtrator_1_tout), .S(SUBTRACAO[1]), .Tout(subtrator_2_tout));
  subtrator subtrator_3 (.A(A[2]), .B(B[2]), .T(subtrator_2_tout), .S(SUBTRACAO[2]), .Tout(subtrator_3_tout));
  subtrator subtrator_4 (.A(A[3]), .B(B[3]), .T(subtrator_3_tout), .S(SUBTRACAO[3]), .Tout(subtrator_4_tout));
  subtrator subtrator_5 (.A(A[4]), .B(B[4]), .T(subtrator_4_tout), .S(SUBTRACAO[4]), .Tout(subtrator_5_tout));
  subtrator subtrator_6 (.A(A[5]), .B(B[5]), .T(subtrator_5_tout), .S(SUBTRACAO[5]), .Tout(subtrator_6_tout));
  subtrator subtrator_7 (.A(A[6]), .B(B[6]), .T(subtrator_6_tout), .S(SUBTRACAO[6]), .Tout(subtrator_7_tout));
  subtrator subtrator_8 (.A(A[7]), .B(B[7]), .T(subtrator_7_tout), .S(SUBTRACAO[7]), .Tout(Borrow));

  // Notes on the sheet:
  //   Subtrator 1
  //   Subtrator 2
  //   Subtrator 3
  //   Sutrator 4
  //   Subtrator 5
  //   Subtrator 6
  //   Subtrator 7
  //   Subtrator 8
endmodule

module multiplexador2_1 (
  input  L0,
  input  L1,
  input  S0,
  output y
);

  wire and_1_out, and_2_out, not_1_out;

  not not_1 (not_1_out, S0);
  and and_1 (and_1_out, L0, not_1_out);
  and and_2 (and_2_out, L1, S0);
  or or_1 (y, and_1_out, and_2_out);

  // Notes on the sheet:
  //   SO
endmodule

module multiplexador (
  input  [7:0] I0,
  input  [7:0] I1,
  input  [7:0] I2,
  input  [7:0] I3,
  input  [7:0] L4,
  input  [7:0] I5,
  input  [7:0] L6,
  input  [7:0] L7,
  input  S2,
  input  S1,
  input  S0,
  output [7:0] Z
);

  wire [7:0] and_1_out, and_2_out, and_3_out, and_4_out, and_5_out, and_6_out, and_7_out, and_8_out,
       bit_extender_1_out, bit_extender_2_out, bit_extender_3_out, not_1_out, not_2_out, not_3_out,
       not_4_out, not_5_out, not_6_out, not_7_out, not_8_out, not_9_out, not_10_out, not_11_out, not_12_out;

  assign bit_extender_1_out = {{7{S2}}, S2};  // Bit_Extender bit_extender_1
  assign bit_extender_2_out = {{7{S1}}, S1};  // Bit_Extender bit_extender_2
  assign bit_extender_3_out = {{7{S0}}, S0};  // Bit_Extender bit_extender_3
  assign not_1_out = ~bit_extender_1_out;  // NOT_Gate not_1, 8 bits wide
  assign not_2_out = ~bit_extender_2_out;  // NOT_Gate not_2, 8 bits wide
  assign not_3_out = ~bit_extender_3_out;  // NOT_Gate not_3, 8 bits wide
  assign not_4_out = ~bit_extender_1_out;  // NOT_Gate not_4, 8 bits wide
  assign not_5_out = ~bit_extender_2_out;  // NOT_Gate not_5, 8 bits wide
  assign not_6_out = ~bit_extender_1_out;  // NOT_Gate not_6, 8 bits wide
  assign not_7_out = ~bit_extender_3_out;  // NOT_Gate not_7, 8 bits wide
  assign not_8_out = ~bit_extender_1_out;  // NOT_Gate not_8, 8 bits wide
  assign not_9_out = ~bit_extender_2_out;  // NOT_Gate not_9, 8 bits wide
  assign not_10_out = ~bit_extender_3_out;  // NOT_Gate not_10, 8 bits wide
  assign not_11_out = ~bit_extender_2_out;  // NOT_Gate not_11, 8 bits wide
  assign not_12_out = ~bit_extender_3_out;  // NOT_Gate not_12, 8 bits wide
  assign and_1_out = not_1_out & not_2_out & not_3_out & I0;  // AND_Gate and_1, 8 bits wide
  assign and_2_out = not_4_out & not_5_out & I1 & bit_extender_3_out;  // AND_Gate and_2, 8 bits wide
  assign and_3_out = not_6_out & bit_extender_2_out & I2 & not_7_out;  // AND_Gate and_3, 8 bits wide
  assign and_4_out = not_8_out & bit_extender_2_out & I3 & bit_extender_3_out;  // AND_Gate and_4, 8 bits wide
  assign and_5_out = bit_extender_1_out & not_9_out & L4 & not_10_out;  // AND_Gate and_5, 8 bits wide
  assign and_6_out = bit_extender_1_out & not_11_out & I5 & bit_extender_3_out;  // AND_Gate and_6, 8 bits wide
  assign and_7_out = bit_extender_1_out & bit_extender_2_out & L6 & not_12_out;  // AND_Gate and_7, 8 bits wide
  assign and_8_out = bit_extender_1_out & bit_extender_2_out & L7 & bit_extender_3_out;  // AND_Gate and_8, 8 bits wide
  assign Z = and_1_out | and_2_out | and_3_out | and_4_out | and_5_out | and_6_out | and_7_out | and_8_out;  // OR_Gate or_1, 8 bits wide

  // Notes on the sheet:
  //   001
  //   010
  //   011
  //   100
  //   101
  //   110
  //   111
  //   000
endmodule
